# Fritzing sketch lightorgan-8 (saved by Fritzing 0.9.2b)

parts:
  U1 = 8RelayModule
  Part1 = Arduino Nano (Rev3.0)
  Power_plug1 = Power plug

nets:
  N1: U1.IN2, Part1.D4
  N2: U1.IN1, Part1.D3
  GND: U1.GND, Part1.GND, Power_plug1.GND
  VCC: U1.VCC, Part1.5V, Power_plug1.VCC
  N3: U1.IN3, Part1.D5
  N4: U1.IN4, Part1.D2
  N5: U1.IN5, Part1.D9
  N6: U1.IN6, Part1.D6
  N7: U1.IN7, Part1.D8
  N8: U1.IN8, Part1.D7

custom parts:
  8RelayModule: 8 relay arduino module SONGLE SRD05VDC-SL-C
